// Logisim project Program counter.circ as structural Verilog: 1 circuit, main circuit Program counter
module Program_counter (
  input  in_1,
  output [15:0] out_2
);

  wire and_1_out, and_2_out, and_3_out, and_4_out, and_5_out, and_6_out, and_7_out, and_8_out, and_9_out,
       and_10_out, and_11_out, and_12_out, and_13_out, and_14_out, and_15_out, clock_1_out;

  and and_1 (and_1_out, in_1, out_2[0]);
  and and_2 (and_2_out, out_2[2], and_3_out);
  Clock clock_1 (.out(clock_1_out));
  and and_3 (and_3_out, and_1_out, out_2[1]);
  J_K_Flip_Flop j_k_ff_1 (.J(in_1), .clk(clock_1_out), .K(in_1), .Q(out_2[0]));  // open: Qn, preset, en, reset
  J_K_Flip_Flop j_k_ff_2 (
    .J(and_1_out), .clk(clock_1_out), .K(and_1_out), .Q(out_2[1]));  // open: Qn, preset, en, reset
  J_K_Flip_Flop j_k_ff_3 (
    .J(and_3_out), .clk(clock_1_out), .K(and_3_out), .Q(out_2[2]));  // open: Qn, preset, en, reset
  J_K_Flip_Flop j_k_ff_4 (
    .J(and_2_out), .clk(clock_1_out), .K(and_2_out), .Q(out_2[3]));  // open: Qn, preset, en, reset
  and and_4 (and_4_out, out_2[4], and_6_out);
  and and_5 (and_5_out, out_2[6], and_7_out);
  and and_6 (and_6_out, and_2_out, out_2[3]);
  and and_7 (and_7_out, and_4_out, out_2[5]);
  J_K_Flip_Flop j_k_ff_5 (
    .J(and_6_out), .clk(clock_1_out), .K(and_6_out), .Q(out_2[4]));  // open: Qn, preset, en, reset
  J_K_Flip_Flop j_k_ff_6 (
    .J(and_4_out), .clk(clock_1_out), .K(and_4_out), .Q(out_2[5]));  // open: Qn, preset, en, reset
  J_K_Flip_Flop j_k_ff_7 (
    .J(and_7_out), .clk(clock_1_out), .K(and_7_out), .Q(out_2[6]));  // open: Qn, preset, en, reset
  J_K_Flip_Flop j_k_ff_8 (
    .J(and_5_out), .clk(clock_1_out), .K(and_5_out), .Q(out_2[7]));  // open: Qn, preset, en, reset
  and and_8 (and_8_out, out_2[8], and_10_out);
  and and_9 (and_9_out, out_2[10], and_11_out);
  and and_10 (and_10_out, and_5_out, out_2[7]);
  and and_11 (and_11_out, and_8_out, out_2[9]);
  J_K_Flip_Flop j_k_ff_9 (
    .J(and_10_out), .clk(clock_1_out), .K(and_10_out), .Q(out_2[8]));  // open: Qn, preset, en, reset
  J_K_Flip_Flop j_k_ff_10 (
    .J(and_8_out), .clk(clock_1_out), .K(and_8_out), .Q(out_2[9]));  // open: Qn, preset, en, reset
  J_K_Flip_Flop j_k_ff_11 (
    .J(and_11_out), .clk(clock_1_out), .K(and_11_out), .Q(out_2[10]));  // open: Qn, preset, en, reset
  J_K_Flip_Flop j_k_ff_12 (
    .J(and_9_out), .clk(clock_1_out), .K(and_9_out), .Q(out_2[11]));  // open: Qn, preset, en, reset
  and and_12 (and_12_out, out_2[12], and_14_out);
  and and_13 (and_13_out, out_2[14], and_15_out);
  and and_14 (and_14_out, and_9_out, out_2[11]);
  and and_15 (and_15_out, and_12_out, out_2[13]);
  J_K_Flip_Flop j_k_ff_13 (
    .J(and_14_out), .clk(clock_1_out), .K(and_14_out), .Q(out_2[12]));  // open: Qn, preset, en, reset
  J_K_Flip_Flop j_k_ff_14 (
    .J(and_12_out), .clk(clock_1_out), .K(and_12_out), .Q(out_2[13]));  // open: Qn, preset, en, reset
  J_K_Flip_Flop j_k_ff_15 (
    .J(and_15_out), .clk(clock_1_out), .K(and_15_out), .Q(out_2[14]));  // open: Qn, preset, en, reset
  J_K_Flip_Flop j_k_ff_16 (
    .J(and_13_out), .clk(clock_1_out), .K(and_13_out), .Q(out_2[15]));  // open: Qn, preset, en, reset
endmodule
