// Logisim project RAM.circ as structural Verilog: 5 circuits, main circuit RAM
module RAM (
  input  [19:0] in_1,
  input  [19:0] in_2,
  input  [3:0] Data,
  input  [19:0] in_4,
  input  [1:0] Address,
  input  R_W,
  input  [19:0] in_7,
  output [19:0] out_8,
  output [3:0] Output
);

  wire memory_cell_1_output, memory_cell_2_output, memory_cell_3_output, memory_cell_4_output,
       memory_cell_5_output, memory_cell_6_output, memory_cell_7_output, memory_cell_8_output,
       memory_cell_9_output, memory_cell_10_output, memory_cell_11_output, memory_cell_12_output,
       memory_cell_13_output, memory_cell_14_output, memory_cell_15_output, memory_cell_16_output,
       n2x4_decoder_1_output_0, n2x4_decoder_1_output_1, n2x4_decoder_1_output_2, n2x4_decoder_1_output_3,
       undriven, undriven_2, undriven_3, undriven_4, undriven_5, undriven_6, undriven_7, undriven_8,
       undriven_9, undriven_10;
  wire [19:0] or_5_out, or_6_out, or_8_out, or_9_out, or_10_out, or_11_out, or_12_out, or_13_out, or_14_out,
       or_15_out, or_16_out, or_17_out, or_18_out, or_19_out, or_20_out, or_21_out, or_22_out, or_23_out,
       or_24_out, or_25_out, or_26_out, or_27_out, word_1_output, word_2_output, word_3_output,
       word_4_output, word_5_output, word_6_output, word_7_output, word_8_output;

  _2x4_decoder u_2x4_decoder_1 (
    .Input_a(Address[1]), .Input_b(Address[0]), .Output_0(n2x4_decoder_1_output_0),
    .Output_1(n2x4_decoder_1_output_1), .Output_2(n2x4_decoder_1_output_2), .Output_3(n2x4_decoder_1_output_3));
  Memory_cell memory_cell_1 (
    .Select(n2x4_decoder_1_output_0), .Input(Data[3]), .Output(memory_cell_1_output), .R_W(R_W));
  Memory_cell memory_cell_2 (
    .Select(n2x4_decoder_1_output_1), .Input(Data[3]), .Output(memory_cell_2_output), .R_W(R_W));
  Memory_cell memory_cell_3 (
    .Select(n2x4_decoder_1_output_2), .Input(Data[3]), .Output(memory_cell_3_output), .R_W(R_W));
  Memory_cell memory_cell_4 (
    .Select(n2x4_decoder_1_output_3), .Input(Data[3]), .Output(memory_cell_4_output), .R_W(R_W));
  or or_1 (Output[3], memory_cell_1_output, memory_cell_2_output, memory_cell_3_output, memory_cell_4_output);
  Memory_cell memory_cell_5 (
    .Select(n2x4_decoder_1_output_0), .Input(Data[2]), .Output(memory_cell_5_output), .R_W(R_W));
  Memory_cell memory_cell_6 (
    .Select(n2x4_decoder_1_output_1), .Input(Data[2]), .Output(memory_cell_6_output), .R_W(R_W));
  Memory_cell memory_cell_7 (
    .Select(n2x4_decoder_1_output_2), .Input(Data[2]), .Output(memory_cell_7_output), .R_W(R_W));
  Memory_cell memory_cell_8 (
    .Select(n2x4_decoder_1_output_3), .Input(Data[2]), .Output(memory_cell_8_output), .R_W(R_W));
  or or_2 (Output[2], memory_cell_5_output, memory_cell_6_output, memory_cell_7_output, memory_cell_8_output);
  Memory_cell memory_cell_9 (
    .Select(n2x4_decoder_1_output_0), .Input(Data[1]), .Output(memory_cell_9_output), .R_W(R_W));
  Memory_cell memory_cell_10 (
    .Select(n2x4_decoder_1_output_1), .Input(Data[1]), .Output(memory_cell_10_output), .R_W(R_W));
  Memory_cell memory_cell_11 (
    .Select(n2x4_decoder_1_output_2), .Input(Data[1]), .Output(memory_cell_11_output), .R_W(R_W));
  Memory_cell memory_cell_12 (
    .Select(n2x4_decoder_1_output_3), .Input(Data[1]), .Output(memory_cell_12_output), .R_W(R_W));
  or or_3 (Output[1], memory_cell_9_output, memory_cell_10_output, memory_cell_11_output, memory_cell_12_output);
  Memory_cell memory_cell_13 (
    .Select(n2x4_decoder_1_output_0), .Input(Data[0]), .Output(memory_cell_13_output), .R_W(R_W));
  Memory_cell memory_cell_14 (
    .Select(n2x4_decoder_1_output_1), .Input(Data[0]), .Output(memory_cell_14_output), .R_W(R_W));
  Memory_cell memory_cell_15 (
    .Select(n2x4_decoder_1_output_2), .Input(Data[0]), .Output(memory_cell_15_output), .R_W(R_W));
  Memory_cell memory_cell_16 (
    .Select(n2x4_decoder_1_output_3), .Input(Data[0]), .Output(memory_cell_16_output), .R_W(R_W));
  or or_4 (Output[0], memory_cell_13_output, memory_cell_14_output, memory_cell_15_output, memory_cell_16_output);
  assign or_5_out = in_1 | in_2;  // OR_Gate or_5, 20 bits wide
  assign or_6_out = in_4 | in_7;  // OR_Gate or_6, 20 bits wide
  assign out_8 = or_5_out | or_6_out;  // OR_Gate or_7, 20 bits wide
  Word word_1 (.Select(undriven), .R_W(undriven_6), .Output(word_1_output));  // open: Data
  Word word_2 (.Select(undriven_5), .R_W(undriven_6), .Output(word_2_output));  // open: Data
  Word word_3 (.Select(undriven_2), .R_W(undriven_7), .Output(word_3_output));  // open: Data
  Word word_4 (.Select(undriven_4), .R_W(undriven_7), .Output(word_4_output));  // open: Data
  Word word_5 (.Select(undriven_8), .R_W(undriven_6), .Output(word_5_output));  // open: Data
  Word word_6 (.Select(undriven_9), .R_W(undriven_6), .Output(word_6_output));  // open: Data
  Word word_7 (.Select(undriven_3), .R_W(undriven_7), .Output(word_7_output));  // open: Data
  Word word_8 (.Select(undriven_10), .R_W(undriven_7), .Output(word_8_output));  // open: Data
  // OR_Gate or_8 has open pins: out=or_8_out
  // OR_Gate or_9 has open pins: out=or_9_out
  // OR_Gate or_10 has open pins: out=or_10_out
  // OR_Gate or_11 has open pins: out=or_11_out
  // OR_Gate or_12 has open pins: out=or_12_out
  // OR_Gate or_13 has open pins: out=or_13_out
  // OR_Gate or_14 has open pins: out=or_14_out
  // OR_Gate or_15 has open pins: out=or_15_out
  // OR_Gate or_16 has open pins: out=or_16_out
  // OR_Gate or_17 has open pins: out=or_17_out
  // OR_Gate or_18 has open pins: out=or_18_out
  // OR_Gate or_19 has open pins: out=or_19_out
  // OR_Gate or_20 has open pins: out=or_20_out
  // OR_Gate or_21 has open pins: out=or_21_out
  // OR_Gate or_22 has open pins: out=or_22_out
  // OR_Gate or_23 has open pins: out=or_23_out
  assign or_24_out = or_8_out | or_9_out | or_10_out | or_11_out;  // OR_Gate or_24, 20 bits wide
  assign or_25_out = or_12_out | or_13_out | or_14_out | or_15_out;  // OR_Gate or_25, 20 bits wide
  assign or_26_out = or_16_out | or_17_out | or_18_out | or_19_out;  // OR_Gate or_26, 20 bits wide
  assign or_27_out = or_20_out | or_21_out | or_22_out | or_23_out;  // OR_Gate or_27, 20 bits wide
  // OR_Gate or_28 has open pins: in0=or_24_out, in1=or_25_out, in2=or_26_out, in3=or_27_out, out=open
endmodule

module Word (
  input  [19:0] Data,
  input  Select,
  input  R_W,
  output [19:0] Output
);

  wire undriven;

  Memory_cell memory_cell_1 (.Select(Select), .Input(Data[19]), .Output(Output[19]), .R_W(undriven));
  Memory_cell memory_cell_2 (.Select(Select), .Input(Data[18]), .Output(Output[18]), .R_W(undriven));
  Memory_cell memory_cell_3 (.Select(Select), .Input(Data[17]), .Output(Output[17]), .R_W(R_W));
  Memory_cell memory_cell_4 (.Select(Select), .Input(Data[16]), .Output(Output[16]), .R_W(R_W));
  Memory_cell memory_cell_5 (.Select(Select), .Input(Data[15]), .Output(Output[15]), .R_W(R_W));
  Memory_cell memory_cell_6 (.Select(Select), .Input(Data[14]), .Output(Output[14]), .R_W(R_W));
  Memory_cell memory_cell_7 (.Select(Select), .Input(Data[13]), .Output(Output[13]), .R_W(R_W));
  Memory_cell memory_cell_8 (.Select(Select), .Input(Data[12]), .Output(Output[12]), .R_W(R_W));
  Memory_cell memory_cell_9 (.Select(Select), .Input(Data[11]), .Output(Output[11]), .R_W(R_W));
  Memory_cell memory_cell_10 (.Select(Select), .Input(Data[10]), .Output(Output[10]), .R_W(R_W));
  Memory_cell memory_cell_11 (.Select(Select), .Input(Data[9]), .Output(Output[9]), .R_W(R_W));
  Memory_cell memory_cell_12 (.Select(Select), .Input(Data[8]), .Output(Output[8]), .R_W(R_W));
  Memory_cell memory_cell_13 (.Select(Select), .Input(Data[7]), .Output(Output[7]), .R_W(R_W));
  Memory_cell memory_cell_14 (.Select(Select), .Input(Data[6]), .Output(Output[6]), .R_W(R_W));
  Memory_cell memory_cell_15 (.Select(Select), .Input(Data[5]), .Output(Output[5]), .R_W(R_W));
  Memory_cell memory_cell_16 (.Select(Select), .Input(Data[4]), .Output(Output[4]), .R_W(R_W));
  Memory_cell memory_cell_17 (.Select(Select), .Input(Data[3]), .Output(Output[3]), .R_W(R_W));
  Memory_cell memory_cell_18 (.Select(Select), .Input(Data[2]), .Output(Output[2]), .R_W(R_W));
  Memory_cell memory_cell_19 (.Select(Select), .Input(Data[1]), .Output(Output[1]), .R_W(R_W));
  Memory_cell memory_cell_20 (.Select(Select), .Input(Data[0]), .Output(Output[0]), .R_W(R_W));
endmodule

module _2x4_decoder (
  input  Input_a,
  input  Input_b,
  output Output_0,
  output Output_1,
  output Output_2,
  output Output_3
);

  wire not_1_out, not_2_out;

  not not_1 (not_1_out, Input_a);
  not not_2 (not_2_out, Input_b);
  and and_1 (Output_0, not_1_out, not_2_out);
  and and_2 (Output_1, not_1_out, Input_b);
  and and_3 (Output_2, Input_a, not_2_out);
  and and_4 (Output_3, Input_a, Input_b);
endmodule

module Memory_cell (
  input  Select,
  input  Input,
  input  R_W,
  output Output
);

  wire and_1_out, and_2_out, not_1_out, not_2_out, sr_latch_1_output;

  not not_1 (not_1_out, Input);
  and and_1 (and_1_out, Select, not_2_out, not_1_out);
  and and_2 (and_2_out, Select, not_2_out, Input);
  not not_2 (not_2_out, R_W);
  SR_latch sr_latch_1 (.Set(and_1_out), .Reset(and_2_out), .Output(sr_latch_1_output));
  and and_3 (Output, Select, sr_latch_1_output, R_W);
endmodule

module SR_latch (
  input  Set,
  input  Reset,
  output Output
);

  wire nor_2_out;

  nor nor_1 (Output, Set, nor_2_out);
  nor nor_2 (nor_2_out, Output, Reset);
endmodule
